// Logisim project CO.circ as structural Verilog: 1 circuit, main circuit main
module main (
  input  NOT_GATE,
  input  in_2,
  input  in_3,
  input  in_4,
  input  in_5,
  input  in_6,
  input  in_7,
  input  in_8,
  input  in_9,
  input  in_10,
  input  in_11,
  input  in_12,
  input  in_13,
  input  in_14,
  input  in_15,
  input  in_16,
  input  in_17,
  input  in_18,
  input  in_19,
  input  in_20,
  input  in_21,
  input  in_22,
  input  in_23,
  input  in_24,
  input  in_25,
  input  NOR_GATE,
  input  in_27,
  input  in_28,
  input  in_29,
  input  in_30,
  input  in_31,
  input  in_32,
  input  in_33,
  input  XOR_GATE,
  input  in_35,
  input  in_36,
  input  in_37,
  input  in_38,
  input  in_39,
  input  in_40,
  input  in_41,
  input  XNOR_GATE,
  input  in_43,
  input  in_44,
  input  in_45,
  input  in_46,
  input  in_47,
  input  in_48,
  input  in_49,
  output out_50,
  output out_51,
  output out_52,
  output out_53,
  output out_54,
  output out_55,
  output out_56,
  output out_57,
  output out_58,
  output out_59,
  output out_60,
  output out_61,
  output out_62,
  output out_63,
  output out_64,
  output out_65,
  output out_66,
  output out_67,
  output out_68,
  output out_69,
  output out_70,
  output out_71,
  output out_72,
  output out_73,
  output out_74
);

  not not_1 (out_50, NOT_GATE);
  and and_1 (out_51, in_2, in_6);
  or or_1 (out_55, in_10, in_14);
  nand nand_1 (out_59, in_18, in_22);
  nor nor_1 (out_63, NOR_GATE, in_30);
  xor xor_1 (out_67, XOR_GATE, in_38);
  xnor xnor_1 (out_71, XNOR_GATE, in_46);
  and and_2 (out_52, in_3, in_7);
  or or_2 (out_56, in_11, in_15);
  nand nand_2 (out_60, in_19, in_23);
  nor nor_2 (out_64, in_27, in_31);
  xor xor_2 (out_68, in_35, in_39);
  xnor xnor_2 (out_72, in_43, in_47);
  and and_3 (out_53, in_4, in_8);
  or or_3 (out_57, in_12, in_16);
  nand nand_3 (out_61, in_20, in_24);
  nor nor_3 (out_65, in_28, in_32);
  xor xor_3 (out_69, in_36, in_40);
  xnor xnor_3 (out_73, in_44, in_48);
  and and_4 (out_54, in_5, in_9);
  or or_4 (out_58, in_13, in_17);
  nand nand_4 (out_62, in_21, in_25);
  nor nor_4 (out_66, in_29, in_33);
  xor xor_4 (out_70, in_37, in_41);
  xnor xnor_4 (out_74, in_45, in_49);

  // Notes on the sheet:
  //                 AND GATE
  //           OR GATE
  //            NAND GATE
  //   WORK BY -NANDANI SINGH
endmodule
